// Digital circuit plantilla.dig as structural Verilog
module plantilla (
  input  [4:0] N1,
  input  [4:0] N2,
  input  [4:0] N3,
  input  [4:0] N4,
  input  [4:0] N5,
  input  [4:0] N6,
  input  [4:0] N7,
  input  [4:0] N8,
  input  [4:0] N9,
  input  [4:0] N10,
  input  plus,
  output out_12
);

  wire [4:0] neg_1_out, neg_2_out, neg_3_out, neg_4_out, neg_5_out, neg_11_out, neg_12_out, neg_13_out,
       neg_14_out, neg_15_out;
  wire [7:0] neg_6_out, neg_7_out, neg_8_out, neg_9_out, neg_10_out, neg_16_out, neg_17_out, neg_18_out,
       neg_19_out, neg_20_out;
  wire [7:7] undriven, undriven_2, undriven_3, undriven_4, undriven_5, undriven_6, undriven_7, undriven_8,
       undriven_9, undriven_10;

  Add #(.Bits(5)) add_1 (.c_i(1'b0));  // open: a, b, s, c_o
  Neg #(.Bits(5)) neg_1 (.in(N1), .out(neg_1_out));
  Neg #(.Bits(5)) neg_2 (.in(N2), .out(neg_2_out));
  Neg #(.Bits(5)) neg_3 (.in(N3), .out(neg_3_out));
  Neg #(.Bits(5)) neg_4 (.in(N4), .out(neg_4_out));
  Neg #(.Bits(5)) neg_5 (.in(N5), .out(neg_5_out));
  Neg #(.Bits(8)) neg_6 (.in({3'b000, neg_1_out}), .out(neg_6_out));
  Neg #(.Bits(8)) neg_7 (.in({3'b000, neg_2_out}), .out(neg_7_out));
  Neg #(.Bits(8)) neg_8 (.in({3'b000, neg_3_out}), .out(neg_8_out));
  Neg #(.Bits(8)) neg_9 (.in({3'b000, neg_4_out}), .out(neg_9_out));
  Neg #(.Bits(8)) neg_10 (.in({3'b000, neg_5_out}), .out(neg_10_out));
  Multiplexer #(.Bits(8)) multiplexer_1 (
    .sel(N1[4]), .in_0({undriven_5[7], {3{N1[4]}}, N1[3:0]}), .in_1(neg_6_out));  // open: out
  Multiplexer #(.Bits(8)) multiplexer_2 (
    .sel(N2[4]), .in_0({undriven[7], {3{N2[4]}}, N2[3:0]}), .in_1(neg_7_out));  // open: out
  Multiplexer #(.Bits(8)) multiplexer_3 (
    .sel(N3[4]), .in_0({undriven_2[7], {3{N3[4]}}, N3[3:0]}), .in_1(neg_8_out));  // open: out
  Multiplexer #(.Bits(8)) multiplexer_4 (
    .sel(N4[4]), .in_0({undriven_3[7], {3{N4[4]}}, N4[3:0]}), .in_1(neg_9_out));  // open: out
  Multiplexer #(.Bits(8)) multiplexer_5 (
    .sel(N5[4]), .in_0({undriven_4[7], {3{N5[4]}}, N5[3:0]}), .in_1(neg_10_out));  // open: out
  Neg #(.Bits(5)) neg_11 (.in(N6), .out(neg_11_out));
  Neg #(.Bits(5)) neg_12 (.in(N7), .out(neg_12_out));
  Neg #(.Bits(5)) neg_13 (.in(N8), .out(neg_13_out));
  Neg #(.Bits(5)) neg_14 (.in(N9), .out(neg_14_out));
  Neg #(.Bits(5)) neg_15 (.in(N10), .out(neg_15_out));
  Neg #(.Bits(8)) neg_16 (.in({3'b000, neg_11_out}), .out(neg_16_out));
  Neg #(.Bits(8)) neg_17 (.in({3'b000, neg_12_out}), .out(neg_17_out));
  Neg #(.Bits(8)) neg_18 (.in({3'b000, neg_13_out}), .out(neg_18_out));
  Neg #(.Bits(8)) neg_19 (.in({3'b000, neg_14_out}), .out(neg_19_out));
  Neg #(.Bits(8)) neg_20 (.in({3'b000, neg_15_out}), .out(neg_20_out));
  Multiplexer #(.Bits(8)) multiplexer_6 (
    .sel(N6[4]), .in_0({undriven_6[7], {3{N6[4]}}, N6[3:0]}), .in_1(neg_16_out));  // open: out
  Multiplexer #(.Bits(8)) multiplexer_7 (
    .sel(N7[4]), .in_0({undriven_7[7], {3{N7[4]}}, N7[3:0]}), .in_1(neg_17_out));  // open: out
  Multiplexer #(.Bits(8)) multiplexer_8 (
    .sel(N8[4]), .in_0({undriven_8[7], {3{N8[4]}}, N8[3:0]}), .in_1(neg_18_out));  // open: out
  Multiplexer #(.Bits(8)) multiplexer_9 (
    .sel(N9[4]), .in_0({undriven_9[7], {3{N9[4]}}, N9[3:0]}), .in_1(neg_19_out));  // open: out
  Multiplexer #(.Bits(8)) multiplexer_10 (
    .sel(N10[4]), .in_0({undriven_10[7], {3{N10[4]}}, N10[3:0]}), .in_1(neg_20_out));  // open: out
  // also tied to GND on the sheet: {N1[4], N2[4], N3[4], N4[4], N5[4], N6[4], N7[4], N8[4], N9[4], N10[4]}
endmodule
