// Digital circuit Ejercicio7segmentos.dig as structural Verilog
module Ejercicio7segmentos (
  input  [4:0] in_1
);

  Seven_Seg seven_seg_1 ();  // open: a, b, c, d, e, f, g, dp
  Seven_Seg seven_seg_2 ();  // open: a, b, c, d, e, f, g, dp
  Seven_Seg seven_seg_3 ();  // open: a, b, c, d, e, f, g, dp
endmodule
