// Digital circuit BoardGame.dig as structural Verilog
module BoardGame (
  input  [4:0] in_4,
  input  [4:0] in_5,
  input  [3:0] in_7,
  input  clk,
  input  in_9,
  output [7:0] out_1,
  output [7:0] out_2,
  output [7:0] out_3,
  output [4:0] out_6,
  output [4:0] out_10,
  output [4:0] out_11,
  output [4:0] out_12,
  output [4:0] out_13,
  output [4:0] out_14,
  output [4:0] out_15,
  output [4:0] out_16,
  output [4:0] out_17,
  output [4:0] out_18,
  output [4:0] out_19
);

  wire and_1_out, and_2_out, and_3_out, and_4_out, button_1_out, button_2_out, button_3_out, not_1_out,
       not_2_out, not_3_out, Signo, u_RandomGenerator_2_numbergenerated, u_RandomGenerator_3_numbergenerated,
       u_RandomGenerator_4_numbergenerated, u_RandomGenerator_5_numbergenerated,
       u_RandomGenerator_6_numbergenerated, u_RandomGenerator_18_numbergenerated,
       u_RandomGenerator_19_numbergenerated, u_RandomGenerator_numbergenerated;
  wire [4:0] neg_1_out, neg_2_out, neg_3_out, neg_4_out, neg_5_out, neg_6_out, neg_7_out, neg_8_out,
       neg_9_out, neg_10_out;
  wire [7:0] add_1_s, add_2_s, add_3_s, add_4_s, add_5_s, add_6_s, add_7_s, add_8_s, add_9_s, add_10_s,
       add_11_s, add_12_s, add_13_s, add_14_s, add_15_s, add_16_s, add_17_s, add_18_s, multiplexer_11_out,
       multiplexer_12_out, multiplexer_13_out, multiplexer_14_out, multiplexer_15_out, multiplexer_16_out,
       multiplexer_17_out, multiplexer_18_out, multiplexer_19_out, multiplexer_20_out, multiplexer_21_out,
       multiplexer_22_out, multiplexer_23_out, multiplexer_24_out, multiplexer_25_out, multiplexer_26_out,
       multiplexer_27_out, multiplexer_28_out, multiplexer_29_out, multiplexer_30_out, multiplexer_31_out,
       n1_t, n2_t, n3_t, n4_t, n5_t, n6_t, n7_t, n8_t, n9_t, n10_t, neg_11_out, neg_12_out, neg_13_out,
       neg_14_out, neg_15_out, neg_16_out, neg_17_out, neg_18_out, neg_19_out, neg_20_out, u_ABC_letra,
       u_ASCII_letra;

  RandomGenerator #(.applicationType("IVERILOG")) u_RandomGenerator (
    .pulse(clk), .numberGenerated(u_RandomGenerator_numbergenerated));
  RandomGenerator #(.applicationType("IVERILOG")) u_RandomGenerator_2 (
    .pulse(u_RandomGenerator_numbergenerated), .numberGenerated(u_RandomGenerator_2_numbergenerated));
  RandomGenerator #(.applicationType("IVERILOG")) u_RandomGenerator_3 (
    .pulse(u_RandomGenerator_2_numbergenerated), .numberGenerated(u_RandomGenerator_3_numbergenerated));
  RandomGenerator #(.applicationType("IVERILOG")) u_RandomGenerator_4 (
    .pulse(u_RandomGenerator_3_numbergenerated), .numberGenerated(u_RandomGenerator_4_numbergenerated));
  RandomGenerator #(.applicationType("IVERILOG")) u_RandomGenerator_5 (
    .pulse(clk), .numberGenerated(u_RandomGenerator_5_numbergenerated));
  RandomGenerator #(.applicationType("IVERILOG")) u_RandomGenerator_6 (
    .pulse(clk), .numberGenerated(u_RandomGenerator_6_numbergenerated));
  RandomGenerator #(.applicationType("IVERILOG")) u_RandomGenerator_7 (.pulse(clk), .numberGenerated(Signo));
  RandomGenerator #(.applicationType("IVERILOG")) u_RandomGenerator_8 (.pulse(clk), .numberGenerated(out_10));
  RandomGenerator #(.applicationType("IVERILOG")) u_RandomGenerator_9 (.pulse(clk), .numberGenerated(out_11));
  RandomGenerator #(.applicationType("IVERILOG")) u_RandomGenerator_10 (.pulse(clk), .numberGenerated(out_12));
  RandomGenerator #(.applicationType("IVERILOG")) u_RandomGenerator_11 (.pulse(clk), .numberGenerated(out_13));
  not not_1 (not_1_out, u_RandomGenerator_6_numbergenerated);
  RandomGenerator #(.applicationType("IVERILOG")) u_RandomGenerator_12 (
    .pulse(u_RandomGenerator_numbergenerated), .numberGenerated(out_14));
  RandomGenerator #(.applicationType("IVERILOG")) u_RandomGenerator_13 (
    .pulse(u_RandomGenerator_2_numbergenerated), .numberGenerated(out_15));
  RandomGenerator #(.applicationType("IVERILOG")) u_RandomGenerator_14 (
    .pulse(u_RandomGenerator_3_numbergenerated), .numberGenerated(out_16));
  RandomGenerator #(.applicationType("IVERILOG")) u_RandomGenerator_15 (
    .pulse(u_RandomGenerator_4_numbergenerated), .numberGenerated(out_17));
  RandomGenerator #(.applicationType("IVERILOG")) u_RandomGenerator_16 (
    .pulse(u_RandomGenerator_5_numbergenerated), .numberGenerated(out_18));
  RandomGenerator #(.applicationType("IVERILOG")) u_RandomGenerator_17 (.pulse(not_1_out), .numberGenerated(out_19));
  Neg #(.Bits(5)) neg_1 (.in(out_10), .out(neg_1_out));
  Neg #(.Bits(5)) neg_2 (.in(out_11), .out(neg_2_out));
  Neg #(.Bits(5)) neg_3 (.in(out_12), .out(neg_3_out));
  Neg #(.Bits(5)) neg_4 (.in(out_13), .out(neg_4_out));
  Neg #(.Bits(5)) neg_5 (.in(out_14), .out(neg_5_out));
  Neg #(.Bits(5)) neg_6 (.in(out_15), .out(neg_6_out));
  Neg #(.Bits(5)) neg_7 (.in(out_16), .out(neg_7_out));
  Neg #(.Bits(5)) neg_8 (.in(out_17), .out(neg_8_out));
  Neg #(.Bits(5)) neg_9 (.in(out_18), .out(neg_9_out));
  Neg #(.Bits(5)) neg_10 (.in(out_19), .out(neg_10_out));
  Neg #(.Bits(8)) neg_11 (.in({3'b000, neg_1_out}), .out(neg_11_out));
  Neg #(.Bits(8)) neg_12 (.in({3'b000, neg_2_out}), .out(neg_12_out));
  Neg #(.Bits(8)) neg_13 (.in({3'b000, neg_3_out}), .out(neg_13_out));
  Neg #(.Bits(8)) neg_14 (.in({3'b000, neg_4_out}), .out(neg_14_out));
  Neg #(.Bits(8)) neg_15 (.in({3'b000, neg_5_out}), .out(neg_15_out));
  Neg #(.Bits(8)) neg_16 (.in({3'b000, neg_6_out}), .out(neg_16_out));
  Neg #(.Bits(8)) neg_17 (.in({3'b000, neg_7_out}), .out(neg_17_out));
  Neg #(.Bits(8)) neg_18 (.in({3'b000, neg_8_out}), .out(neg_18_out));
  Neg #(.Bits(8)) neg_19 (.in({3'b000, neg_9_out}), .out(neg_19_out));
  Neg #(.Bits(8)) neg_20 (.in({3'b000, neg_10_out}), .out(neg_20_out));
  Multiplexer #(.Bits(8)) multiplexer_1 (.sel(out_10[4]), .in_0({3'b000, out_10}), .in_1(neg_11_out), .out(n1_t));
  Multiplexer #(.Bits(8)) multiplexer_2 (.sel(out_11[4]), .in_0({3'b000, out_11}), .in_1(neg_12_out), .out(n2_t));
  Multiplexer #(.Bits(8)) multiplexer_3 (.sel(out_12[4]), .in_0({3'b000, out_12}), .in_1(neg_13_out), .out(n3_t));
  Multiplexer #(.Bits(8)) multiplexer_4 (.sel(out_13[4]), .in_0({3'b000, out_13}), .in_1(neg_14_out), .out(n4_t));
  Multiplexer #(.Bits(8)) multiplexer_5 (.sel(out_14[4]), .in_0({3'b000, out_14}), .in_1(neg_15_out), .out(n5_t));
  Multiplexer #(.Bits(8)) multiplexer_6 (.sel(out_15[4]), .in_0({3'b000, out_15}), .in_1(neg_16_out), .out(n6_t));
  Multiplexer #(.Bits(8)) multiplexer_7 (.sel(out_16[4]), .in_0({3'b000, out_16}), .in_1(neg_17_out), .out(n7_t));
  Multiplexer #(.Bits(8)) multiplexer_8 (.sel(out_17[4]), .in_0({3'b000, out_17}), .in_1(neg_18_out), .out(n8_t));
  Multiplexer #(.Bits(8)) multiplexer_9 (.sel(out_18[4]), .in_0({3'b000, out_18}), .in_1(neg_19_out), .out(n9_t));
  Multiplexer #(.Bits(8)) multiplexer_10 (.sel(out_19[4]), .in_0({3'b000, out_19}), .in_1(neg_20_out), .out(n10_t));
  Multiplexer #(.Bits(8)) multiplexer_11 (.sel(n1_t[7]), .in_0(n1_t), .in_1({8{1'b0}}), .out(multiplexer_11_out));
  Multiplexer #(.Bits(8)) multiplexer_12 (.sel(n2_t[7]), .in_0(n2_t), .in_1({8{1'b0}}), .out(multiplexer_12_out));
  Multiplexer #(.Bits(8)) multiplexer_13 (.sel(n3_t[7]), .in_0(n3_t), .in_1({8{1'b0}}), .out(multiplexer_13_out));
  Multiplexer #(.Bits(8)) multiplexer_14 (.sel(n4_t[7]), .in_0(n4_t), .in_1({8{1'b0}}), .out(multiplexer_14_out));
  Multiplexer #(.Bits(8)) multiplexer_15 (.sel(n5_t[7]), .in_0(n5_t), .in_1({8{1'b0}}), .out(multiplexer_15_out));
  Multiplexer #(.Bits(8)) multiplexer_16 (.sel(n6_t[7]), .in_0(n6_t), .in_1({8{1'b0}}), .out(multiplexer_16_out));
  Multiplexer #(.Bits(8)) multiplexer_17 (.sel(n7_t[7]), .in_0(n7_t), .in_1({8{1'b0}}), .out(multiplexer_17_out));
  Multiplexer #(.Bits(8)) multiplexer_18 (.sel(n8_t[7]), .in_0(n8_t), .in_1({8{1'b0}}), .out(multiplexer_18_out));
  Multiplexer #(.Bits(8)) multiplexer_19 (.sel(n9_t[7]), .in_0(n9_t), .in_1({8{1'b0}}), .out(multiplexer_19_out));
  Multiplexer #(.Bits(8)) multiplexer_20 (.sel(n10_t[7]), .in_0(n10_t), .in_1({8{1'b0}}), .out(multiplexer_20_out));
  Multiplexer #(.Bits(8)) multiplexer_21 (.sel(n1_t[7]), .in_0({8{1'b0}}), .in_1(n1_t), .out(multiplexer_21_out));
  Multiplexer #(.Bits(8)) multiplexer_22 (.sel(n2_t[7]), .in_0({8{1'b0}}), .in_1(n2_t), .out(multiplexer_22_out));
  Multiplexer #(.Bits(8)) multiplexer_23 (.sel(n3_t[7]), .in_0({8{1'b0}}), .in_1(n3_t), .out(multiplexer_23_out));
  Multiplexer #(.Bits(8)) multiplexer_24 (.sel(n4_t[7]), .in_0({8{1'b0}}), .in_1(n4_t), .out(multiplexer_24_out));
  Multiplexer #(.Bits(8)) multiplexer_25 (.sel(n5_t[7]), .in_0({8{1'b0}}), .in_1(n5_t), .out(multiplexer_25_out));
  Multiplexer #(.Bits(8)) multiplexer_26 (.sel(n6_t[7]), .in_0({8{1'b0}}), .in_1(n6_t), .out(multiplexer_26_out));
  Multiplexer #(.Bits(8)) multiplexer_27 (.sel(n7_t[7]), .in_0({8{1'b0}}), .in_1(n7_t), .out(multiplexer_27_out));
  Multiplexer #(.Bits(8)) multiplexer_28 (.sel(n8_t[7]), .in_0({8{1'b0}}), .in_1(n8_t), .out(multiplexer_28_out));
  Multiplexer #(.Bits(8)) multiplexer_29 (.sel(n9_t[7]), .in_0({8{1'b0}}), .in_1(n9_t), .out(multiplexer_29_out));
  Multiplexer #(.Bits(8)) multiplexer_30 (.sel(n10_t[7]), .in_0({8{1'b0}}), .in_1(n10_t), .out(multiplexer_30_out));
  Add #(.Bits(8)) add_1 (.a(multiplexer_11_out), .b(multiplexer_12_out), .c_i(1'b0), .s(add_1_s));  // open: c_o
  Add #(.Bits(8)) add_2 (.a(multiplexer_13_out), .b(multiplexer_14_out), .c_i(1'b0), .s(add_2_s));  // open: c_o
  Add #(.Bits(8)) add_3 (.a(multiplexer_15_out), .b(multiplexer_16_out), .c_i(1'b0), .s(add_3_s));  // open: c_o
  Add #(.Bits(8)) add_4 (.a(multiplexer_17_out), .b(multiplexer_18_out), .c_i(1'b0), .s(add_4_s));  // open: c_o
  Add #(.Bits(8)) add_5 (.a(multiplexer_19_out), .b(multiplexer_20_out), .c_i(1'b0), .s(add_5_s));  // open: c_o
  Add #(.Bits(8)) add_6 (.a(multiplexer_21_out), .b(multiplexer_22_out), .c_i(1'b0), .s(add_6_s));  // open: c_o
  Add #(.Bits(8)) add_7 (.a(multiplexer_23_out), .b(multiplexer_24_out), .c_i(1'b0), .s(add_7_s));  // open: c_o
  Add #(.Bits(8)) add_8 (.a(multiplexer_25_out), .b(multiplexer_26_out), .c_i(1'b0), .s(add_8_s));  // open: c_o
  Add #(.Bits(8)) add_9 (.a(multiplexer_27_out), .b(multiplexer_28_out), .c_i(1'b0), .s(add_9_s));  // open: c_o
  Add #(.Bits(8)) add_10 (.a(multiplexer_29_out), .b(multiplexer_30_out), .c_i(1'b0), .s(add_10_s));  // open: c_o
  Add #(.Bits(8)) add_11 (.a(add_1_s), .b(add_2_s), .c_i(1'b0), .s(add_11_s));  // open: c_o
  Add #(.Bits(8)) add_12 (.a(add_3_s), .b(add_4_s), .c_i(1'b0), .s(add_12_s));  // open: c_o
  Add #(.Bits(8)) add_13 (.a(add_6_s), .b(add_7_s), .c_i(1'b0), .s(add_13_s));  // open: c_o
  Add #(.Bits(8)) add_14 (.a(add_8_s), .b(add_9_s), .c_i(1'b0), .s(add_14_s));  // open: c_o
  Add #(.Bits(8)) add_15 (.a(add_11_s), .b(add_12_s), .c_i(1'b0), .s(add_15_s));  // open: c_o
  Add #(.Bits(8)) add_16 (.a(add_13_s), .b(add_14_s), .c_i(1'b0), .s(add_16_s));  // open: c_o
  RandomGenerator #(.applicationType("IVERILOG")) u_RandomGenerator_18 (
    .pulse(clk), .numberGenerated(u_RandomGenerator_18_numbergenerated));
  Add #(.Bits(8)) add_17 (.a(add_15_s), .b(add_5_s), .c_i(1'b0), .s(add_17_s));  // open: c_o
  not not_2 (not_2_out, Signo);
  Add #(.Bits(8)) add_18 (.a(add_16_s), .b(add_10_s), .c_i(1'b0), .s(add_18_s));  // open: c_o
  RandomGenerator #(.applicationType("IVERILOG")) u_RandomGenerator_19 (
    .pulse(Signo), .numberGenerated(u_RandomGenerator_19_numbergenerated));
  and and_1 (and_1_out, not_2_out, u_RandomGenerator_19_numbergenerated);
  and and_2 (and_2_out, Signo, u_RandomGenerator_18_numbergenerated);
  Multiplexer #(.Bits(8)) multiplexer_31 (.sel(and_2_out), .in_0(add_18_s), .in_1({8{1'b0}}), .out(multiplexer_31_out));
  Neg #(.Bits(8)) neg_21 (.in(multiplexer_31_out), .out(out_2));
  Multiplexer #(.Bits(8)) multiplexer_32 (.sel(and_1_out), .in_0(add_17_s), .in_1({8{1'b0}}), .out(out_1));
  Button button_1 (.out(button_1_out));
  Button button_2 (.out(button_2_out));
  Button button_3 (.out(button_3_out));
  ARRAY #(.applicationType("IVERILOG")) u_ARRAY (.pos(in_4), .salida(out_3));
  BubbleSort #(.applicationType("IVERILOG")) u_BubbleSort (
    .dato(in_5), .pos(in_7), .almacenar(button_3_out), .ordenar(button_2_out), .show(button_1_out),
    .resultado(out_6));
  not not_3 (not_3_out, in_9);
  and and_3 (and_3_out, clk, in_9);
  and and_4 (and_4_out, not_3_out, clk);
  ASCII #(.applicationType("IVERILOG")) u_ASCII (.clockcito(and_3_out), .letra(u_ASCII_letra));
  ABC #(.applicationType("IVERILOG")) u_ABC (.clockcito(and_4_out), .letra(u_ABC_letra));
  Terminal terminal_1 (.D(u_ASCII_letra), .C(and_3_out), .en(1'b1));
  Terminal terminal_2 (.D(u_ABC_letra), .C(and_4_out), .en(1'b1));

  // Other names for the same wires on the sheet: N1[4:0] = out_10; N2[4:0] = out_11; N3[4:0] = out_12;
  //   N4[4:0] = out_13; N5[4:0] = out_14; N6[4:0] = out_15; N7[4:0] = out_16; N8[4:0] = out_17; N9[4:0] = out_18;
  //   N10[4:0] = out_19; warp = clk
endmodule

/* Code of RandomGenerator:
module RandomGenerator(
    input pulse,
    output reg numberGenerated
);

initial begin
    numberGenerated = 0;
end

always @ (pulse)
begin
    numberGenerated = $urandom_range(0,1);
end
    
    
endmodule
*/

/* Code of RandomGenerator:
module RandomGenerator(
    input pulse,
    output reg [4:0] numberGenerated
);

initial begin
    numberGenerated = 0;
end

always @ (pulse)
begin
    numberGenerated = $urandom % 31;
end
    
    
endmodule
*/

/* Code of RandomGenerator:
module RandomGenerator(
    input pulse,
    output reg [4:0] numberGenerated
);

initial begin
    numberGenerated = 0;
end

always @ (pulse)
begin
    numberGenerated = $urandom_range(0, 31);
end
    
    
endmodule
*/

/* Code of RandomGenerator:
module RandomGenerator(
    input pulse,
    output reg [4:0] numberGenerated
);

reg [4:0] i;
reg [4:0] j;

initial begin
    numberGenerated = 0;
    i = 0;
    j = 0;
end

always @ (pulse)
begin
    i = $urandom_range(0, 16);
    j = $urandom_range(0, 15);
    numberGenerated = i + j;
end
    
    
endmodule
*/

/* Code of RandomGenerator:
module RandomGenerator(
    input pulse,
    output reg [4:0] numberGenerated
);

reg [4:0] i;
reg [4:0] j;

initial begin
    numberGenerated = 0;
    i = 0;
    j = 0;
end

always @ (pulse)
begin
    i = $urandom_range(0, 8);
    j = $urandom_range(0, 15);
    numberGenerated = (i*2) + j;
end
    
    
endmodule
*/

/* Code of RandomGenerator:
module RandomGenerator(
    input pulse,
    output reg numberGenerated
);

initial begin
    numberGenerated = 1;
end

always @ (pulse)
begin
    numberGenerated = $urandom_range(0,1);
end
    
    
endmodule
*/

/* Code of ARRAY:
module ARRAY(
    input [4:0] pos,
    output reg [7:0] salida
);
    //data         //array size
reg [7:0] vector [5:0];

initial begin
    vector [0] = 56;
    vector [1] = 189;
    vector [2] = 190;
    vector [3] = 221;
    vector [4] = 155;
    vector [5] = 235;

end

always @ (*)
begin
    salida = vector[pos];
end

endmodule
*/

/* Code of BubbleSort:
module BubbleSort(
    input [4:0] dato,
    input [3:0] pos,
    input almacenar,
    input ordenar,    
    input show,
    output reg [4:0]resultado
);
    //data         //array size
reg [4:0] vector [15:0];
// temp
reg [4:0] temporal;

//variables para el ciclo 
reg [3:0] i;
reg [3:0] j;

initial begin
    vector [0] = 0;
    vector [1] = 0;
    vector [2] = 0;
    vector [3] = 0;
    vector [4] = 0;
    vector [5] = 0;
    vector [6] = 0;
    vector [7] = 0;
    vector [8] = 0;
    vector [9] = 0;
    vector [10] = 0;
    vector [11] = 0;
    vector [12] = 0;
    vector [13] = 0;
    vector [14] = 0;
    vector [15] = 0;
end

always @ (posedge almacenar) begin
    vector[pos] = dato;
    resultado = vector[pos];
end

always @ (posedge show) begin
    resultado = vector[pos];
end

always @ (pos) begin
    resultado = vector[pos];
end

always @ (posedge ordenar) begin
    
    for (i = 0; i < 16 - 1; i++)
    begin

        // Last i elements are already in place
        for (j = 0; j < 16 - i - 1; j++)
        begin
            if (vector[j] > vector[j + 1])
            begin
                temporal = vector[j];
                vector[j] = vector[j + 1];
                vector[j + 1] = temporal;
                
            end
        end
    end  
end

endmodule
*/

/* Code of ASCII:
module ASCII(
    input clockcito,
    output reg [7:0] letra
);

//variable de letra
reg [7:0] R;

always @ (posedge clockcito) begin
    
    R = $urandom % 127;
    letra = R;
end
endmodule
*/

/* Code of ABC:
module ABC(
    input clockcito,
    output reg [7:0] letra
);

//variable de letra
reg [7:0] R;

always @ (posedge clockcito) begin
    
    R = $urandom % 3;
    if(R == 1)
    begin
        letra = 65;
    end
    else if( R == 2)
    begin
        letra = 66;
    end
    else
    begin
        letra = 67;
    end
    
end
endmodule
*/
